# Fritzing sketch obs-macro-scene-switcher (saved by Fritzing 0.9.3b)

parts:
  Part2 = Arduino Micro (Rev3)
  S1 = Pushbutton [package="[SMD]"]
  S2 = Pushbutton [package="[SMD]"]
  S3 = Pushbutton [package="[SMD]"]
  S4 = Pushbutton [package="[SMD]"]
  S5 = Pushbutton [package="[SMD]"]

nets:
  N1: Part2.GND, Part2.D6_PWM/A7, S1.Pin_3, S1.Pin_4
  N2: Part2.D2/SDA, S5.Pin_3, S5.Pin_4
  N3: Part2.D3/SCL, S4.Pin_3, S4.Pin_4
  N4: Part2.D4_PWM/A6, S3.Pin_3, S3.Pin_4
  N5: Part2.D5_PWM, S2.Pin_3, S2.Pin_4
